# Fritzing sketch Pico_Schimmel (saved by Fritzing 0.9.6b)
circuit board: 9cm x 5cm
circuit board: 2.5cm x 2.5cm
circuit board: 1.4cm x 1cm
breadboards: 1

parts:
  Mod1 = Raspberry Pi Pico
  DS18B20 = male pin header, 3 pins [form="♂ (male)"]
  J1 = male pin header, 4 pins [form="♂ (male)"]
  J2 = male pin header, 4 pins [form="♂ (male)"]
  R2 = Resistor [tolerance=±5% resistance=4.7k power=0.25 package=THT]

nets:
  N1: Mod1.pin_1, J1.pin4
  N2: Mod1.pin_2, J1.pin3
  N3: Mod1.pin_3, Mod1.pin_8, Mod1.pin_13, Mod1.pin_18, Mod1.pin_23, Mod1.pin_28, Mod1.pin_33, Mod1.pin_38, Mod1.pin_42, DS18B20.pin3, J1.pin2, J2.pin1
  N4: Mod1.pin_19, J2.pin4
  N5: Mod1.pin_20, J2.pin3
  N6: Mod1.pin_21, DS18B20.pin2, R2.Pin_0
  N7: Mod1.pin_36, DS18B20.pin1, J1.pin1, J2.pin2, R2.Pin_1

notes:
  GND
  VIN
  SCL
  SDA
  BME280
  Pin1
  Pin20
  Linux
  im
  Handwerk

custom parts:
  Raspberry Pi Pico: Raspberry Pi Pico. Based around the RP2040 microcontroller the Pico is a low cost microcontroller device bringing Raspberry Pi quality, cost, and easy of use to the microcontroller space. Jan 2021, Split part in to two versions: tht (this one) and SMD. This one will drill holes for a .1 in header in pcb to allow plugging in the module as well as providing pads to solder the module to the top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
